# Fritzing sketch BarCocktail (saved by Fritzing 0.9.3b)
breadboards: 1

parts:
  LED1 = LED - 5mm [color="Blue (430nm)" package="5 mm [THT]"]  # not connected
  R1 = Resistor [tolerance=±5% resistance=220 package=THT]
  LED2 = LED - 5mm [color="Blue (430nm)" package="5 mm [THT]"]  # not connected
  R2 = Resistor [tolerance=±5% resistance=220 package=THT]
  LED3 = LED - 5mm [color="Blue (430nm)" package="5 mm [THT]"]  # not connected
  R3 = Resistor [tolerance=±5% resistance=220 package=THT]
  LED4 = LED - 5mm [color="Blue (430nm)" package="5 mm [THT]"]  # not connected
  R4 = Resistor [tolerance=±5% resistance=220 package=THT]
  LED5 = LED - 5mm [color="Blue (430nm)" package="5 mm [THT]"]
  R5 = Resistor [tolerance=±5% resistance=220 package=THT]
  LED6 = LED - 5mm [color="Blue (430nm)" package="5 mm [THT]"]  # not connected
  R6 = Resistor [tolerance=±5% resistance=220 package=THT]
  LED7 = LED - 5mm [color="Blue (430nm)" package="5 mm [THT]"]  # not connected
  R7 = Resistor [tolerance=±5% resistance=220 package=THT]
  Composant1 = Arduino Uno (Rev3)
  LED9 = LED - 5mm [color="Blue (430nm)" package="5 mm [THT]"]  # not connected
  R9 = Resistor [tolerance=±5% resistance=220 package=THT]
  Relay_Module_8ports = 8RelayModule
  Power_plug1 = Power plug [part_number=12V]
  Pompe_1 = DC Motor
  Pompe_2 = DC Motor
  Pompe_3 = DC Motor
  Pompe_4 = DC Motor
  Pompe_5 = DC Motor
  Pompe_6 = DC Motor
  Pompe_7 = DC Motor
  Pompe_8 = DC Motor
  Bouton_Haut = Momentary Switch [package=ksa_sealed_tac_switch]
  R10 = Resistor [tolerance=±5% resistance=10k package=THT]
  Bouton_Bas = Momentary Switch [package=ksa_sealed_tac_switch]
  R11 = Resistor [tolerance=±5% resistance=10k package=THT]
  U1 = LCD-16X2 [package=lcd-16x2]
  R12 = Trimmer Potentiometer [maximum_resistance=10kΩ package=THT]
  R13 = Resistor [tolerance=±5% resistance=220 package=THT]
  Composant2 = Arduino Nano (Rev3.0)
  Nokia_5110_LCD_Module1 = Nokia 5110 LCD
  Bouton_Select = Momentary Switch [package=ksa_sealed_tac_switch]
  R14 = Resistor [tolerance=±5% resistance=10k package=THT]
  RGB_Strip_LED1 = RGB Strip LED
  Power_Supp_5V = Power plug
  Composant3 = 12 NeoPixel Ring [part_number=1643]

nets:
  N1: R1.Pin_0, R1.Pin_1, Composant1.D7
  N2: R2.Pin_0, R2.Pin_1, Composant1.D6_PWM
  N3: R3.Pin_0, R3.Pin_1, Composant1.D5_PWM
  N4: R4.Pin_0, R4.Pin_1, Composant1.D4
  N5: LED5.cathode, R5.Pin_0, R5.Pin_1, Composant1.D3_PWM
  GND: LED5.anode, Composant1.GND, Relay_Module_8ports.GND, R10.Pin_1, R11.Pin_1, U1.VSS, U1.R_W, U1.DB0, U1.DB1, U1.DB2, U1.DB3, U1.K, R12.leg1, R14.Pin_1
  N6: R6.Pin_0, R6.Pin_1, Composant1.D2
  N7: R7.Pin_0, R7.Pin_1, Composant1.D1/TX
  N8: Composant1.A0, U1.RS
  N9: Composant1.A1, U1.E
  N10: Composant1.A2, U1.DB4
  N11: Composant1.A3, U1.DB5
  N12: Composant1.A4/SDA, U1.DB6
  N13: Composant1.A5/SCL, U1.DB7
  N14: Composant1.D8, R9.Pin_0, R9.Pin_1
  N15: Composant1.D9_PWM, Bouton_Haut.1, Bouton_Haut.2, R10.Pin_0
  N16: Composant1.D10_PWM/SS, Bouton_Bas.1, Bouton_Bas.2, R11.Pin_0
  N17: Composant1.D11_PWM/MOSI, Bouton_Select.1, Bouton_Select.2, R14.Pin_0
  5V: Composant1.5V, Relay_Module_8ports.VCC, Bouton_Haut.3, Bouton_Haut.4, Bouton_Bas.3, Bouton_Bas.4, U1.VDD, R12.leg2, R13.Pin_1, Bouton_Select.3, Bouton_Select.4
  N18: Relay_Module_8ports.CC1, Pompe_1.pin_2
  N19: Relay_Module_8ports.CC2, Pompe_2.pin_2
  N20: Relay_Module_8ports.CC3, Pompe_3.pin_2
  N21: Relay_Module_8ports.CC4, Pompe_4.pin_2
  N22: Relay_Module_8ports.NC8, Power_plug1.GND
  N23: Relay_Module_8ports.CC5, Pompe_5.pin_2
  N24: Relay_Module_8ports.CC6, Pompe_6.pin_2
  N25: Relay_Module_8ports.CC7, Pompe_7.pin_2
  N26: Relay_Module_8ports.CC8, Pompe_8.pin_2
  N27: Power_plug1.VCC, Pompe_1.pin_1
  N28: U1.VO, R12.wiper
  N29: U1.A, R13.Pin_0
  GND_2: Composant2.GND, Nokia_5110_LCD_Module1.SCLK_(out), Nokia_5110_LCD_Module1.LED_(out), RGB_Strip_LED1.Blue_Connect, Power_Supp_5V.GND, Composant3.GND
  N30: Composant2.D8, Nokia_5110_LCD_Module1.D/C_(out)
  N31: Composant2.D9, Nokia_5110_LCD_Module1.RST_(out)
  N32: Composant2.D10, Nokia_5110_LCD_Module1.SCE_(out)
  N33: Composant2.D11/MOSI, Nokia_5110_LCD_Module1.GND_(out)
  N34: Composant2.D12/MISO, Nokia_5110_LCD_Module1.VCC_(out)
  VIN: Composant2.VIN, RGB_Strip_LED1.Common_Connect, Power_Supp_5V.VCC, Composant3.VDD
  N35: Composant2.5V, Nokia_5110_LCD_Module1.DN(MODI)_(out)
  N36: Composant2.A7, RGB_Strip_LED1.Green_Connect
  N37: Composant2.A6, RGB_Strip_LED1.Red_Connect
  N38: Composant2.A5, Composant3.IN

custom parts:
  8RelayModule: 8 relay arduino module SONGLE SRD05VDC-SL-C
  Nokia 5110 LCD: Nokia 5110 Graphic 84*48 LCD module such as the Sparkfun LCD-10168 or the clones from Ebay. There is example code for the Arduino available from the Sparkfun site in https://learn.sparkfun.com/tutorials/graphic-lcd-hookup-guide This is a 3.3V device, if you are running it from a 5V micro you need a 5V tolorant level translator such as the 74ahc367 to protect the signal imputs. Rafa G. did a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
  RGB Strip LED: A tri-color Strip LED with red, green and blue. Based on LED SMD 5050 RGB Pin order: common cathode - green - red - blue
  12 NeoPixel Ring: 12 ultra bright smart LED NeoPixels are arranged in a circle with 1.5" (37mm) outer diameter. The rings are 'chainable' - connect the output pin of one to the input pin of another. Use only one microcontroller pin to control as many as you can chain together! Each LED is addressable as the driver chip is inside the LED. Each one has ~18mA constant current drive so the color will be very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
